// Logisim project procesadorMonociclo.circ as structural Verilog: 11 circuits, main circuit main
module main (
  output [31:0] out_1,
  output [31:0] out_2,
  output [31:0] out_3,
  output [31:0] out_4,
  output [31:0] out_5,
  output [31:0] out_6,
  output [5:0] out_7,
  output [5:0] out_8,
  output [31:0] out_9,
  output [31:0] out_10,
  output [31:0] out_11,
  output [31:0] out_12,
  output [31:0] out_13,
  output [31:0] out_14,
  output [5:0] out_15,
  output [5:0] out_16,
  output [31:0] out_17,
  output [4:0] out_18,
  output [31:0] out_19,
  output [31:0] out_20,
  output [31:0] out_21,
  output [31:0] out_22,
  output [4:0] out_23,
  output [31:0] out_24,
  output [3:0] out_25
);

  wire alu1_1_zero, and_1_out, clock_1_out, control_init_1_aluop0, control_init_1_aluop1,
       control_init_1_alusrc, control_init_1_branch, control_init_1_jal, control_init_1_jumpp,
       control_init_1_memread, control_init_1_memtoreg, control_init_1_memwrite, control_init_1_regdst,
       control_init_1_regwrite, jrcontrol_1_jr;
  wire [4:0] multiplexer_1_out;
  wire [31:0] adder_1_out, shifter_1_out;

  Clock clock_1 (.out(clock_1_out));
  fetch fetch_1 (
    .pcnext(out_2), .clk(clock_1_out), .pcplus({out_3[31:28], out_4[27:0]}), .instructionnnn(out_10));  // open: reset, out_6
  JRcontrol jrcontrol_1 (.opcode(out_7), .funct(out_3[7:2]), .jr(jrcontrol_1_jr));
  // Probe on out_23
  brkdwn brkdwn_1 (
    .instruction(out_10), .funct(out_3[7:2]), .shamt(out_3[12:8]), .rd(out_3[17:13]), .rt(out_3[22:18]),
    .rs(out_3[27:23]), .opcode(out_7));
  Multiplexer #(.width(5)) multiplexer_1 (
    .in0(out_3[22:18]), .in1({5{1'b1}}), .out(multiplexer_1_out), .sel(control_init_1_jal));
  Multiplexer #(.width(32)) multiplexer_2 (
    .in0(out_24), .in1({out_3[31:28], out_4[27:0]}), .out(out_19), .sel(control_init_1_jal));
  Multiplexer #(.width(5)) multiplexer_3 (
    .in0(multiplexer_1_out), .in1(out_3[17:13]), .out(out_23), .sel(control_init_1_regdst));
  // Probe on {out_3[31:2], 2'b00}
  Shifter #(.width(32)) shifter_1 (.in({{16{1'b0}}, out_3[17:2]}), .\dist (5'b00010), .out(shifter_1_out));
  Adder #(.width(32)) adder_1 (
    .a({out_3[31:28], out_4[27:0]}), .b(shifter_1_out), .out(adder_1_out));  // open: cin, cout
  and and_1 (and_1_out, control_init_1_branch, alu1_1_zero);
  control_init control_init_1 (
    .opCode(out_7), .regDst(control_init_1_regdst), .ALUSrc(control_init_1_alusrc),
    .memtoreg(control_init_1_memtoreg), .regwrite(control_init_1_regwrite), .memread(control_init_1_memread),
    .MemWrite(control_init_1_memwrite), .Branch(control_init_1_branch), .Aluop1(control_init_1_aluop1),
    .aluop0(control_init_1_aluop0), .Jumpp(control_init_1_jumpp), .jal(control_init_1_jal));
  banco_registros banco_registros_1 (
    .clk(clock_1_out), .writedata(out_19), .Register1(out_3[27:23]), .Register2(out_3[22:18]),
    .Regwrt(control_init_1_regwrite), .writeRegister(out_23), .readData1(out_5), .readData2(out_20));
  ALUcontrol alucontrol_1 (
    .op1(control_init_1_aluop1), .op0(control_init_1_aluop0), .func(out_3[7:2]), .Alucontroll(out_25));
  Multiplexer #(.width(32)) multiplexer_4 (
    .in0({out_3[31:28], out_4[27:0]}), .in1(adder_1_out), .out(out_6), .sel(and_1_out));
  Multiplexer #(.width(32)) multiplexer_5 (
    .in0(out_6), .in1({out_3[31:2], 2'b00}), .out(out_1), .sel(control_init_1_jumpp));
  Multiplexer #(.width(32)) multiplexer_6 (
    .in0(out_20), .in1({{16{1'b0}}, out_3[17:2]}), .out(out_22), .sel(control_init_1_alusrc));
  Alu1 alu1_1 (.A(out_5), .B(out_22), .ALUcnTrl(out_25), .RESULT(out_11), .ZERO(alu1_1_zero));
  Multiplexer #(.width(32)) multiplexer_7 (.in0(out_1), .in1(out_5), .out(out_2), .sel(jrcontrol_1_jr));
  // Probe on out_11
  Multiplexer #(.width(32)) multiplexer_8 (.in0(out_11), .in1(out_21), .out(out_24), .sel(control_init_1_memtoreg));
  data_memory data_memory_1 (
    .address(out_11), .memwrite(control_init_1_memwrite), .memread(control_init_1_memread),
    .clk(clock_1_out), .writedata(out_20), .read_data(out_21));

  assign out_3[1:0] = 2'b00;
  assign out_4[31:28] = out_3[31:28];
  assign out_8 = out_7;
  assign out_9 = {out_3[31:28], out_4[27:0]};
  assign out_12 = {out_3[31:28], out_4[27:0]};
  assign out_13 = out_5;
  assign out_14 = out_5;
  assign out_15 = out_3[7:2];
  assign out_16 = out_7;
  assign out_17 = {out_3[31:28], out_4[27:0]};
  assign out_18 = out_3[27:23];
endmodule

module PC (
  input  [31:0] entradaIN,
  input  clock,
  input  reinicio,
  output [31:0] out_4
);

  Register #(.width(32)) register_1 (.D(entradaIN), .en(clock), .clk(clock), .Q(out_4), .clr(reinicio));
endmodule

module add (
  input  [31:0] entrada_pc,
  output [31:0] out_2
);

  Adder #(.width(32)) adder_1 (.a(entrada_pc), .b(32'h4), .out(out_2));  // open: cin, cout
endmodule

module banco_registros (
  input  clk,
  input  [31:0] writedata,
  input  [4:0] Register1,
  input  [4:0] Register2,
  input  Regwrt,
  input  [4:0] writeRegister,
  output [31:0] readData1,
  output [31:0] readData2
);

  wire and_1_out, and_2_out, and_3_out, and_4_out, and_5_out, and_6_out, and_7_out, and_8_out, and_9_out,
       and_10_out, and_11_out, and_12_out, and_13_out, and_14_out, and_15_out, and_16_out, and_17_out,
       and_18_out, and_19_out, and_20_out, and_21_out, and_22_out, and_23_out, and_24_out, and_25_out,
       and_26_out, and_27_out, and_28_out, and_29_out, and_30_out, and_31_out, and_32_out;
  wire [31:0] decoder_1_out0, R0_q, R1_q, R2_q, R3_q, R4_q, R5_q, R6_q, R7_q, R8_q, R9_q, R10_q, R11_q,
       R12_q, R13_q, R14_q, R15_q, R16_q, R17_q, R18_q, R19_q, R20_q, R21_q, R22_q, R23_q, R24_q, R25_q,
       R26_q, R27_q, R28_q, R29_q, R30_q, R31_q;

  Decoder #(.enable("false"), .select(5)) decoder_1 (
    .out0(decoder_1_out0[0]), .out1(decoder_1_out0[1]), .out2(decoder_1_out0[2]), .out3(decoder_1_out0[3]),
    .out4(decoder_1_out0[4]), .out5(decoder_1_out0[5]), .out6(decoder_1_out0[6]), .out7(decoder_1_out0[7]),
    .out8(decoder_1_out0[8]), .out9(decoder_1_out0[9]), .out10(decoder_1_out0[10]),
    .out11(decoder_1_out0[11]), .out12(decoder_1_out0[12]), .out13(decoder_1_out0[13]),
    .out14(decoder_1_out0[14]), .out15(decoder_1_out0[15]), .out16(decoder_1_out0[16]),
    .out17(decoder_1_out0[17]), .out18(decoder_1_out0[18]), .out19(decoder_1_out0[19]),
    .out20(decoder_1_out0[20]), .out21(decoder_1_out0[21]), .out22(decoder_1_out0[22]),
    .out23(decoder_1_out0[23]), .out24(decoder_1_out0[24]), .out25(decoder_1_out0[25]),
    .out26(decoder_1_out0[26]), .out27(decoder_1_out0[27]), .out28(decoder_1_out0[28]),
    .out29(decoder_1_out0[29]), .out30(decoder_1_out0[30]), .out31(decoder_1_out0[31]), .sel(writeRegister));
  and and_1 (and_1_out, decoder_1_out0[0], Regwrt);
  and and_2 (and_2_out, decoder_1_out0[1], Regwrt);
  and and_3 (and_3_out, decoder_1_out0[2], Regwrt);
  and and_4 (and_4_out, decoder_1_out0[3], Regwrt);
  and and_5 (and_5_out, decoder_1_out0[4], Regwrt);
  and and_6 (and_6_out, decoder_1_out0[5], Regwrt);
  and and_7 (and_7_out, decoder_1_out0[6], Regwrt);
  and and_8 (and_8_out, decoder_1_out0[7], Regwrt);
  and and_9 (and_9_out, decoder_1_out0[8], Regwrt);
  and and_10 (and_10_out, decoder_1_out0[9], Regwrt);
  and and_11 (and_11_out, decoder_1_out0[10], Regwrt);
  and and_12 (and_12_out, decoder_1_out0[11], Regwrt);
  and and_13 (and_13_out, decoder_1_out0[12], Regwrt);
  and and_14 (and_14_out, decoder_1_out0[13], Regwrt);
  and and_15 (and_15_out, decoder_1_out0[14], Regwrt);
  and and_16 (and_16_out, decoder_1_out0[15], Regwrt);
  and and_17 (and_17_out, decoder_1_out0[16], Regwrt);
  and and_18 (and_18_out, decoder_1_out0[17], Regwrt);
  and and_19 (and_19_out, decoder_1_out0[18], Regwrt);
  and and_20 (and_20_out, decoder_1_out0[19], Regwrt);
  and and_21 (and_21_out, decoder_1_out0[20], Regwrt);
  and and_22 (and_22_out, decoder_1_out0[21], Regwrt);
  and and_23 (and_23_out, decoder_1_out0[22], Regwrt);
  and and_24 (and_24_out, decoder_1_out0[23], Regwrt);
  and and_25 (and_25_out, decoder_1_out0[24], Regwrt);
  and and_26 (and_26_out, decoder_1_out0[25], Regwrt);
  and and_27 (and_27_out, decoder_1_out0[26], Regwrt);
  and and_28 (and_28_out, decoder_1_out0[27], Regwrt);
  and and_29 (and_29_out, decoder_1_out0[28], Regwrt);
  and and_30 (and_30_out, decoder_1_out0[29], Regwrt);
  and and_31 (and_31_out, decoder_1_out0[30], Regwrt);
  and and_32 (and_32_out, decoder_1_out0[31], Regwrt);
  Register #(.width(32)) R0 (.D({32{1'b0}}), .en(and_1_out), .clk(clk), .Q(R0_q));  // open: clr
  Register #(.width(32)) R1 (.D(writedata), .en(and_2_out), .clk(clk), .Q(R1_q));  // open: clr
  Register #(.width(32)) R2 (.D(writedata), .en(and_3_out), .clk(clk), .Q(R2_q));  // open: clr
  Register #(.width(32)) R3 (.D(writedata), .en(and_4_out), .clk(clk), .Q(R3_q));  // open: clr
  Register #(.width(32)) R4 (.D(writedata), .en(and_5_out), .clk(clk), .Q(R4_q));  // open: clr
  Register #(.width(32)) R5 (.D(writedata), .en(and_6_out), .clk(clk), .Q(R5_q));  // open: clr
  Register #(.width(32)) R6 (.D(writedata), .en(and_7_out), .clk(clk), .Q(R6_q));  // open: clr
  Register #(.width(32)) R7 (.D(writedata), .en(and_8_out), .clk(clk), .Q(R7_q));  // open: clr
  Register #(.width(32)) R9 (.D(writedata), .en(and_10_out), .clk(clk), .Q(R9_q));  // open: clr
  Register #(.width(32)) R11 (.D(writedata), .en(and_12_out), .clk(clk), .Q(R11_q));  // open: clr
  Register #(.width(32)) R8 (.D(writedata), .en(and_9_out), .clk(clk), .Q(R8_q));  // open: clr
  Register #(.width(32)) R10 (.D(writedata), .en(and_11_out), .clk(clk), .Q(R10_q));  // open: clr
  Register #(.width(32)) R12 (.D(writedata), .en(and_13_out), .clk(clk), .Q(R12_q));  // open: clr
  Register #(.width(32)) R13 (.D(writedata), .en(and_14_out), .clk(clk), .Q(R13_q));  // open: clr
  Register #(.width(32)) R14 (.D(writedata), .en(and_15_out), .clk(clk), .Q(R14_q));  // open: clr
  Register #(.width(32)) R15 (.D(writedata), .en(and_16_out), .clk(clk), .Q(R15_q));  // open: clr
  Register #(.width(32)) R16 (.D(writedata), .en(and_17_out), .clk(clk), .Q(R16_q));  // open: clr
  Register #(.width(32)) R17 (.D(writedata), .en(and_18_out), .clk(clk), .Q(R17_q));  // open: clr
  Register #(.width(32)) R18 (.D(writedata), .en(and_19_out), .clk(clk), .Q(R18_q));  // open: clr
  Register #(.width(32)) R21 (.D(writedata), .en(and_22_out), .clk(clk), .Q(R21_q));  // open: clr
  Register #(.width(32)) R19 (.D(writedata), .en(and_20_out), .clk(clk), .Q(R19_q));  // open: clr
  Register #(.width(32)) R20 (.D(writedata), .en(and_21_out), .clk(clk), .Q(R20_q));  // open: clr
  Register #(.width(32)) R22 (.D(writedata), .en(and_23_out), .clk(clk), .Q(R22_q));  // open: clr
  Register #(.width(32)) R23 (.D(writedata), .en(and_24_out), .clk(clk), .Q(R23_q));  // open: clr
  Register #(.width(32)) R24 (.D(writedata), .en(and_25_out), .clk(clk), .Q(R24_q));  // open: clr
  Register #(.width(32)) R25 (.D(writedata), .en(and_26_out), .clk(clk), .Q(R25_q));  // open: clr
  Register #(.width(32)) R27 (.D(writedata), .en(and_28_out), .clk(clk), .Q(R27_q));  // open: clr
  Register #(.width(32)) R28 (.D(writedata), .en(and_29_out), .clk(clk), .Q(R28_q));  // open: clr
  Register #(.width(32)) R29 (.D(writedata), .en(and_30_out), .clk(clk), .Q(R29_q));  // open: clr
  Register #(.width(32)) R26 (.D(writedata), .en(and_27_out), .clk(clk), .Q(R26_q));  // open: clr
  Register #(.width(32)) R30 (.D(writedata), .en(and_31_out), .clk(clk), .Q(R30_q));  // open: clr
  Register #(.width(32)) R31 (.D(writedata), .en(and_32_out), .clk(clk), .Q(R31_q));  // open: clr
  Multiplexer #(.select(5), .width(32)) multiplexer_1 (
    .in0(R0_q), .in1(R1_q), .in2(R2_q), .in3(R3_q), .in4(R4_q), .in5(R5_q), .in6(R6_q), .in7(R7_q),
    .in8(R8_q), .in9(R9_q), .in10(R10_q), .in11(R11_q), .in12(R12_q), .in13(R13_q), .in14(R14_q),
    .in15(R15_q), .in16(R16_q), .in17(R17_q), .in18(R18_q), .in19(R19_q), .in20(R20_q), .in21(R21_q),
    .in22(R22_q), .in23(R23_q), .in24(R24_q), .in25(R25_q), .in26(R26_q), .in27(R27_q), .in28(R28_q),
    .in29(R29_q), .in30(R30_q), .in31(R31_q), .out(readData1), .sel(Register1));
  Multiplexer #(.select(5), .width(32)) multiplexer_2 (
    .in0(R0_q), .in1(R1_q), .in2(R2_q), .in3(R3_q), .in4(R4_q), .in5(R5_q), .in6(R6_q), .in7(R7_q),
    .in8(R8_q), .in9(R9_q), .in10(R10_q), .in11(R11_q), .in12(R12_q), .in13(R13_q), .in14(R14_q),
    .in15(R15_q), .in16(R16_q), .in17(R17_q), .in18(R18_q), .in19(R19_q), .in20(R20_q), .in21(R21_q),
    .in22(R22_q), .in23(R23_q), .in24(R24_q), .in25(R25_q), .in26(R26_q), .in27(R27_q), .in28(R28_q),
    .in29(R29_q), .in30(R30_q), .in31(R31_q), .out(readData2), .sel(Register2));
endmodule

module Alu1 (
  input  [31:0] A,
  input  [31:0] B,
  input  [3:0] ALUcnTrl,
  output [31:0] RESULT,
  output ZERO
);

  wire [0:0] comparator_1_lt;
  wire [31:0] adder_1_out, and_1_out, nor_1_out, or_1_out, subtractor_1_out;

  Adder #(.width(32)) adder_1 (.a(A), .b(B), .out(adder_1_out));  // open: cin, cout
  Subtractor #(.width(32)) subtractor_1 (.a(A), .b(B), .out(subtractor_1_out));  // open: bin, bout
  Comparator #(.width(32)) comparator_1 (.a(A), .b(B), .lt(comparator_1_lt[0]));  // open: gt, eq
  assign and_1_out = A & B;  // AND_Gate and_1, 32 bits wide
  assign or_1_out = A | B;  // OR_Gate or_1, 32 bits wide
  assign nor_1_out = ~(A | B);  // NOR_Gate nor_1, 32 bits wide
  Multiplexer #(.select(4), .width(32)) multiplexer_1 (
    .in0({32{1'b0}}), .in1(or_1_out), .in3(and_1_out), .in4({{31{1'b0}}, comparator_1_lt[0]}),
    .in5(subtractor_1_out), .in6(adder_1_out), .in7(nor_1_out), .out(RESULT), .sel(ALUcnTrl));  // open: in2, in8, in9, in10, in11, in12, in13, in14, in15
  Comparator #(.width(32)) comparator_2 (.a(RESULT), .b({32{1'b0}}), .eq(ZERO));  // open: gt, lt
endmodule

module control_init (
  input  [5:0] opCode,
  output regDst,
  output ALUSrc,
  output memtoreg,
  output regwrite,
  output memread,
  output MemWrite,
  output Branch,
  output Aluop1,
  output aluop0,
  output Jumpp,
  output jal
);

  wire addi_out, jump_out, lh_out, lw_out, not_1_out, not_2_out, not_3_out, not_4_out, Op0not_out,
       Op1not_out, Op2not_out, OP3not_out, Op4not_out, Op5not_out, or_3_out;

  not Op0not (Op0not_out, opCode[0]);
  not Op1not (Op1not_out, opCode[1]);
  not Op2not (Op2not_out, opCode[2]);
  not OP3not (OP3not_out, opCode[3]);
  not Op4not (Op4not_out, opCode[4]);
  not Op5not (Op5not_out, opCode[5]);
  not not_1 (not_1_out, opCode[2]);
  not not_2 (not_2_out, opCode[3]);
  not not_3 (not_3_out, opCode[4]);
  not not_4 (not_4_out, opCode[5]);
  and rtype (Aluop1, Op0not_out, Op1not_out, Op2not_out, OP3not_out, Op4not_out, Op5not_out);
  and lw (lw_out, opCode[0], opCode[1], Op2not_out, OP3not_out, Op4not_out, opCode[5]);
  and sw (MemWrite, opCode[0], opCode[1], Op2not_out, opCode[3], Op4not_out, opCode[5]);
  and addi (addi_out, Op0not_out, Op1not_out, Op2not_out, opCode[3], Op4not_out, Op5not_out);
  and lh (lh_out, opCode[0], Op1not_out, Op2not_out, OP3not_out, Op4not_out, opCode[5]);
  and beq (aluop0, Op0not_out, Op1not_out, opCode[2], OP3not_out, Op4not_out, Op5not_out);
  and jump (jump_out, Op0not_out, opCode[1], Op2not_out, OP3not_out, Op4not_out, Op5not_out);
  and jall (jal, opCode[0], opCode[1], not_1_out, not_2_out, not_3_out, not_4_out);
  or or_1 (ALUSrc, lw_out, MemWrite, addi_out, lh_out);
  or or_2 (memtoreg, lw_out, lh_out);
  or or_3 (or_3_out, Aluop1, lw_out, addi_out, lh_out);
  or or_4 (memread, lw_out, lh_out);
  or or_5 (Jumpp, jump_out, jal);
  or or_6 (regwrite, jal, or_3_out);

  assign Branch = aluop0;
  assign regDst = Aluop1;
endmodule

module ALUcontrol (
  input  op1,
  input  op0,
  input  [5:0] func,
  output [3:0] Alucontroll
);

  wire addr_out, andADD_out, andAND_out, andNOR_out, andOR_out, andR_out, andSLT_out, andSUB_out,
       f100000_out, f100010_out, f100100_out, f100101_out, f100111_out, f101010_out, NORr_out, not_1_out,
       not_2_out, not_3_out, not_4_out, not_5_out, not_6_out, not_7_out, not_8_out, not_9_out, not_10_out,
       not_11_out, not_12_out, not_13_out, not_14_out, not_15_out, not_16_out, not_17_out, not_18_out,
       not_19_out, not_20_out, not_21_out, not_22_out, not_23_out, not_24_out, not_25_out, op00LW_out,
       op01Beq_out, op10_out, ORr_out, sltR_out, sub_out;

  not not_1 (not_1_out, op0);
  not not_2 (not_2_out, op1);
  and op01Beq (op01Beq_out, not_2_out, op0);
  not not_3 (not_3_out, op1);
  and op00LW (op00LW_out, not_3_out, not_4_out);
  not not_4 (not_4_out, op0);
  not not_5 (not_5_out, func[4]);
  not not_6 (not_6_out, func[3]);
  not not_7 (not_7_out, func[2]);
  not not_8 (not_8_out, func[1]);
  not not_9 (not_9_out, func[0]);
  not not_10 (not_10_out, func[4]);
  not not_11 (not_11_out, func[3]);
  not not_12 (not_12_out, func[2]);
  not not_13 (not_13_out, func[0]);
  not not_14 (not_14_out, func[4]);
  not not_15 (not_15_out, func[3]);
  not not_16 (not_16_out, func[1]);
  not not_17 (not_17_out, func[0]);
  not not_18 (not_18_out, func[4]);
  not not_19 (not_19_out, func[3]);
  not not_20 (not_20_out, func[1]);
  not not_21 (not_21_out, func[4]);
  not not_22 (not_22_out, func[2]);
  not not_23 (not_23_out, func[0]);
  not not_24 (not_24_out, func[4]);
  not not_25 (not_25_out, func[3]);
  and op10 (op10_out, op1, not_1_out);
  and f100000 (f100000_out, func[5], not_5_out, not_6_out, not_7_out, not_8_out, not_9_out);
  and f100010 (f100010_out, func[5], not_10_out, not_11_out, not_12_out, func[1], not_13_out);
  and f100100 (f100100_out, func[5], not_14_out, not_15_out, func[2], not_16_out, not_17_out);
  and f100101 (f100101_out, func[5], not_18_out, not_19_out, func[2], not_20_out, func[0]);
  and f101010 (f101010_out, func[5], not_21_out, func[3], not_22_out, func[1], not_23_out);
  and f100111 (f100111_out, func[5], not_24_out, not_25_out, func[2], func[1], func[0]);
  and addr (addr_out, f100000_out, op10_out);
  and sub (sub_out, op10_out, f100010_out);
  and andR (andR_out, op10_out, f100100_out);
  and ORr (ORr_out, op10_out, f100101_out);
  and sltR (sltR_out, op10_out, f101010_out);
  and NORr (NORr_out, op10_out, f100111_out);
  and andADD (andADD_out, op10_out, f100000_out, addr_out);
  and andSUB (andSUB_out, op10_out, f100010_out, sub_out);
  and andAND (andAND_out, op10_out, f100100_out, andR_out);
  and andOR (andOR_out, op10_out, f100101_out, ORr_out);
  and andSLT (andSLT_out, op10_out, f101010_out, sltR_out);
  and andNOR (andNOR_out, op10_out, f100111_out, NORr_out);
  or or_1 (Alucontroll[2], op00LW_out, op01Beq_out, andADD_out, andSUB_out, andNOR_out, andSLT_out);
  or or_2 (Alucontroll[1], op00LW_out, andADD_out, andAND_out, andNOR_out);
  or or_3 (Alucontroll[0], andNOR_out, andOR_out, andAND_out, andSUB_out, op01Beq_out);

  assign Alucontroll[3] = 1'b0;
endmodule

module data_memory (
  input  [31:0] address,
  input  memwrite,
  input  memread,
  input  clk,
  input  [31:0] writedata,
  output [31:0] read_data
);

  RAM #(.addrWidth(24), .dataWidth(32)) ram_1 (
    .addr(address[23:0]), .we(memwrite), .oe(memread), .clk(clk), .din(writedata), .dout(read_data));
endmodule

module fetch (
  input  [31:0] pcnext,
  input  clk,
  input  reset,
  output [31:0] pcplus,
  output [31:0] instructionnnn,
  output [31:0] out_6
);

  PC pc_1 (.entradaIN(pcnext), .clock(clk), .reinicio(reset), .out_4(out_6));
  add add_1 (.entrada_pc(out_6), .out_2(pcplus));
  ROM #(.addrWidth(24), .dataWidth(32)) rom_1 (.addr(out_6[25:2]), .data(instructionnnn));

  // Notes on the sheet:
  //   contents of rom_1 (hex, n*v repeats v):
  //   0 0 1 0 20080001 1 0 2 0 20090002 2 0 3 0 200a0003 3 0 4 0 200b0004 4 0 5 0 200c0005 5 0 6 0
  //   200d0006 6 0 7 0 200e0007 7 0 8 0 200f0008 0 0 9 0 20100009 1 0 1 0 20110001 2 0 2 0 20120002 3 0 3
  //   0 20130003 4 0 4 0 20140004 5 0 5 0 20150005 6 0 6 0 20160006 7 0 7 0 20170007 a4282a 11000001
  //   802820 a8282a 11000001 802820 c02020 c4282a 11000001 802820 c8282a 11000001 802820 1002020 1002820
  //   a4202a 11000001 1002020 a8282a 11000001 1002020 c4202a 11000001 1002020 c8282a 11000001 1002020
  //   1009020 1009820 a4202a 11000001 1002820 a8282a 11000001 1002820 c4202a 11000001 1002820 c8282a
  //   11000001 1002820 1202020 1202820 a4202a 11000001 1202820 a8282a 11000001 1202820 c4202a 11000001
  //   1202820 c8282a 11000001 1202820 1402020 1402820 a4202a 11000001 1402820 a8282a 11000001 1402820
  //   c4202a 11000001 1402820 c8282a 11000001 1402820 1602020 1602820 a4202a 11000001 1602820 a8282a
  //   11000001 1602820 c4202a 11000001 1602820 c8282a 11000001 1602820 8000000
endmodule

module JRcontrol (
  input  [5:0] opcode,
  input  [5:0] funct,
  output jr
);

  wire and_1_out, and_2_out, not_1_out, not_2_out, not_3_out, not_4_out, not_5_out, not_6_out, not_7_out,
       not_8_out, not_9_out, not_10_out, not_11_out;

  not not_1 (not_1_out, opcode[0]);
  not not_2 (not_2_out, opcode[1]);
  not not_3 (not_3_out, opcode[2]);
  and and_1 (and_1_out, not_1_out, not_2_out, not_3_out, not_4_out, not_5_out, not_6_out);
  not not_4 (not_4_out, opcode[3]);
  not not_5 (not_5_out, opcode[4]);
  not not_6 (not_6_out, opcode[5]);
  not not_7 (not_7_out, funct[0]);
  not not_8 (not_8_out, funct[1]);
  not not_9 (not_9_out, funct[2]);
  and and_2 (and_2_out, not_7_out, not_8_out, not_9_out, funct[3], not_10_out, not_11_out);
  not not_10 (not_10_out, funct[4]);
  not not_11 (not_11_out, funct[5]);
  and and_3 (jr, and_1_out, and_2_out);
endmodule

module brkdwn (
  input  [31:0] instruction,
  output [5:0] funct,
  output [4:0] shamt,
  output [4:0] rd,
  output [4:0] rt,
  output [4:0] rs,
  output [5:0] opcode
);


  assign funct = instruction[5:0];
  assign opcode = instruction[31:26];
  assign rd = instruction[15:11];
  assign rs = instruction[25:21];
  assign rt = instruction[20:16];
  assign shamt = instruction[10:6];
endmodule
